// Logisim project jaemin_baek-processor.circ as structural Verilog: 4 circuits, main circuit Processor
module Processor (
);

  wire Clear, Clock, comparator_1_eq, DrALU, DrMEM, DrOFF, DrPC, DrReg, LdA, LdB, LdIR, LdMAR, LdPC, LdZ,
       not_1_out, WrMEM, WrREG, Z;
  wire [1:0] FUNC, RegSel;
  wire [3:0] Reg_num;
  wire [5:0] Opcode;
  wire [23:0] controlled_buffer_1_out, MAR_q;
  wire [31:0] A_q, alu_1_out_4, B_q, bit_extender_1_out, PC_q, ram_1_data, registers_1_data_out;
  wire [31:6] IR_q;
  wire [31:24] controlled_buffer_1_out_2;

  Register #(.width(32)) PC (
    .D({controlled_buffer_1_out_2, controlled_buffer_1_out}), .en(LdPC), .Q(PC_q), .clk(Clock), .clr(Clear));
  assign {controlled_buffer_1_out_2, controlled_buffer_1_out} = DrPC ? PC_q : 32'bz;  // Controlled_Buffer controlled_buffer_1
  Comparator #(.width(32)) comparator_1 (
    .a({controlled_buffer_1_out_2, controlled_buffer_1_out}), .b({32{1'b0}}), .eq(comparator_1_eq));  // open: gt, lt
  Register #(.width(1)) Z_Register (.D(comparator_1_eq), .en(LdZ), .Q(Z), .clk(Clock), .clr(Clear));
  Register #(.width(32)) A (
    .D({controlled_buffer_1_out_2, controlled_buffer_1_out}), .en(LdA), .Q(A_q), .clk(Clock), .clr(Clear));
  Register #(.width(32)) B (
    .D({controlled_buffer_1_out_2, controlled_buffer_1_out}), .en(LdB), .Q(B_q), .clk(Clock), .clr(Clear));
  ALU alu_1 (.FUNC(FUNC), .A(A_q), .B(B_q), .out_4(alu_1_out_4));
  assign {controlled_buffer_1_out_2, controlled_buffer_1_out} = DrALU ? alu_1_out_4 : 32'bz;  // Controlled_Buffer controlled_buffer_2
  State_Machine state_machine_1 (
    .Clock(Clock), .OpCode(Opcode), .Z(Z), .DrREG(DrReg), .DrMEM(DrMEM), .DrALU(DrALU), .DrPC(DrPC),
    .DrOFF(DrOFF), .LdPC(LdPC), .LdIR(LdIR), .LdMAR(LdMAR), .LdA(LdA), .LdB(LdB), .LdZ(LdZ), .WrREG(WrREG),
    .WrMEM(WrMEM), .RegSel(RegSel), .ALU_FUNC(FUNC));
  Registers registers_1 (
    .WrReg(WrREG), .RegSel(Reg_num), .Data_In({controlled_buffer_1_out_2, controlled_buffer_1_out}),
    .Clock(Clock), .Clear(Clear), .Data_Out(registers_1_data_out));
  assign {controlled_buffer_1_out_2, controlled_buffer_1_out} = DrReg ? registers_1_data_out : 32'bz;  // Controlled_Buffer controlled_buffer_3
  Register #(.width(24)) MAR (.D(controlled_buffer_1_out), .en(LdMAR), .Q(MAR_q), .clk(Clock), .clr(Clear));
  RAM #(.addrWidth(24), .dataWidth(32), .bus("separate")) ram_1 (
    .addr(MAR_q), .din({controlled_buffer_1_out_2, controlled_buffer_1_out}), .data(ram_1_data), .str(WrMEM),
    .clk(Clock), .ld(not_1_out), .clr(Clear));  // open: sel
  not not_1 (not_1_out, WrMEM);
  Clock clock_1 (.out(Clock));
  assign {controlled_buffer_1_out_2, controlled_buffer_1_out} = DrMEM ? ram_1_data : 32'bz;  // Controlled_Buffer controlled_buffer_4
  Button button_1 (.out(Clear));
  Register #(.width(32)) IR (
    .D({controlled_buffer_1_out_2, controlled_buffer_1_out}), .en(LdIR), .Q({IR_q, Opcode}), .clk(Clock),
    .clr(Clear));
  Multiplexer #(.select(2), .width(4), .enable("false")) multiplexer_1 (
    .in0(IR_q[9:6]), .in1(IR_q[13:10]), .in2(IR_q[31:28]), .in3(4'b1100), .out(Reg_num), .sel(RegSel));
  assign bit_extender_1_out = {{14{IR_q[31]}}, IR_q[31:14]};  // Bit_Extender bit_extender_1
  assign {controlled_buffer_1_out_2, controlled_buffer_1_out} = DrOFF ? bit_extender_1_out : 32'bz;  // Controlled_Buffer controlled_buffer_5

  // Notes on the sheet:
  //   00 = RX
  //   01 = RY
  //   10 = RZ
  //   11= c
endmodule

module State_Machine (
  input  Clock,
  input  [5:0] OpCode,
  input  Z,
  output DrREG,
  output DrMEM,
  output DrALU,
  output DrPC,
  output DrOFF,
  output LdPC,
  output LdIR,
  output LdMAR,
  output LdA,
  output LdB,
  output LdZ,
  output WrREG,
  output WrMEM,
  output [1:0] RegSel,
  output [1:0] ALU_FUNC
);

  wire chkZ, OpTest;
  wire [1:0] bit_extender_1_out;
  wire [5:0] multiplexer_1_out, register_1_q, rom_1_data, rom_2_data, rom_3_data;

  Register #(.width(6)) register_1 (.D(multiplexer_1_out), .en(Clock), .Q(register_1_q), .clk(Clock));  // open: clr
  Multiplexer #(.select(2), .width(6), .enable("false")) multiplexer_1 (
    .in0(rom_1_data), .in1(rom_2_data), .in2(rom_3_data), .out(multiplexer_1_out), .sel({chkZ, OpTest}));  // open: in3
  ROM #(.addrWidth(6), .dataWidth(25)) rom_1 (
    .addr(register_1_q),
    .data({chkZ, OpTest, ALU_FUNC, RegSel, WrMEM, WrREG, LdZ, LdB, LdA, LdMAR, LdIR, LdPC, DrOFF, DrPC, DrALU, DrMEM, DrREG, rom_1_data}));  // open: sel
  assign bit_extender_1_out = {{1{1'b0}}, Z};  // Bit_Extender bit_extender_1
  ROM #(.addrWidth(6), .dataWidth(6)) rom_2 (.addr(OpCode), .data(rom_2_data));  // open: sel
  ROM #(.addrWidth(2), .dataWidth(6)) rom_3 (.addr(bit_extender_1_out), .data(rom_3_data));  // open: sel

  // Notes on the sheet:
  //   contents of rom_1 (hex, n*v repeats v):
  //   6201 1082 600903 800000 84045 108046 20100 84048 108049 220100 8404b 840c 20100 404e 8804f 1000000
  //   410111 4212 8413 900 0 84056 8417 2118 20080 8405a 841b 211c 40040 a021e 840 1f 82061 40a2 8063
  //   40100 84065 108066 420100 84068 620100
  //   contents of rom_2 (hex, n*v repeats v):
  //   4 7 a d 15 19 1d 1f 20 24 27
  //   contents of rom_3 (hex, n*v repeats v):
  //   14 10
endmodule

module ALU (
  input  [31:0] A,
  input  [31:0] B,
  input  [1:0] FUNC,
  output [31:0] out_4
);

  wire [31:0] adder_1_out, adder_2_out, nand_1_out, subtractor_1_out;

  Adder #(.width(32)) adder_1 (.a(A), .b(B), .out(adder_1_out));  // open: cin, cout
  assign nand_1_out = ~(A & B);  // NAND_Gate nand_1, 32 bits wide
  Multiplexer #(.select(2), .width(32), .enable("false")) multiplexer_1 (
    .in0(adder_1_out), .in1(nand_1_out), .in2(subtractor_1_out), .in3(adder_2_out), .out(out_4), .sel(FUNC));
  Subtractor #(.width(32)) subtractor_1 (.a(A), .b(B), .out(subtractor_1_out));  // open: bin, bout
  Adder #(.width(32)) adder_2 (.a(A), .b(32'h1), .out(adder_2_out));  // open: cin, cout
endmodule

// Reg File
module Registers (
  input  WrReg,
  input  [3:0] RegSel,
  input  [31:0] Data_In,
  input  Clock,
  input  Clear,
  output [31:0] Data_Out
);

  wire and_1_out, and_2_out, and_3_out, and_4_out, and_5_out, and_6_out, and_7_out, and_8_out, and_9_out,
       and_10_out, and_11_out, and_12_out, and_13_out, and_14_out, and_15_out, and_16_out, decoder_1_out0,
       decoder_1_out1, decoder_1_out2, decoder_1_out3, decoder_1_out4, decoder_1_out5, decoder_1_out6,
       decoder_1_out7, decoder_1_out8, decoder_1_out9, decoder_1_out10, decoder_1_out11, decoder_1_out12,
       decoder_1_out13, decoder_1_out14, decoder_1_out15;
  wire [31:0] a0, a1, a2, at, fp, k0, ra, s0, s1, s2, sp, t0, t1, t2, v0, zero;

  Decoder #(.select(4), .enable("false")) decoder_1 (
    .out0(decoder_1_out0), .out1(decoder_1_out1), .out2(decoder_1_out2), .out3(decoder_1_out3),
    .out4(decoder_1_out4), .out5(decoder_1_out5), .out6(decoder_1_out6), .out7(decoder_1_out7),
    .out8(decoder_1_out8), .out9(decoder_1_out9), .out10(decoder_1_out10), .out11(decoder_1_out11),
    .out12(decoder_1_out12), .out13(decoder_1_out13), .out14(decoder_1_out14), .out15(decoder_1_out15),
    .sel(RegSel));
  and and_1 (and_1_out, decoder_1_out0, WrReg);
  and and_2 (and_2_out, decoder_1_out1, WrReg);
  and and_3 (and_3_out, decoder_1_out2, WrReg);
  and and_4 (and_4_out, decoder_1_out3, WrReg);
  and and_5 (and_5_out, decoder_1_out4, WrReg);
  and and_6 (and_6_out, decoder_1_out5, WrReg);
  and and_7 (and_7_out, decoder_1_out6, WrReg);
  and and_8 (and_8_out, decoder_1_out7, WrReg);
  and and_9 (and_9_out, decoder_1_out8, WrReg);
  and and_10 (and_10_out, decoder_1_out9, WrReg);
  and and_11 (and_11_out, decoder_1_out10, WrReg);
  and and_12 (and_12_out, decoder_1_out11, WrReg);
  and and_13 (and_13_out, decoder_1_out12, WrReg);
  and and_14 (and_14_out, decoder_1_out13, WrReg);
  and and_15 (and_15_out, decoder_1_out14, WrReg);
  and and_16 (and_16_out, decoder_1_out15, WrReg);
  Register #(.width(32)) u_zero (.D(Data_In), .en(and_1_out), .Q(zero), .clk(Clock), .clr(1'b1));
  Register #(.width(32)) u_at (.D(Data_In), .en(and_2_out), .Q(at), .clk(Clock), .clr(Clear));
  Register #(.width(32)) u_v0 (.D(Data_In), .en(and_3_out), .Q(v0), .clk(Clock), .clr(Clear));
  Register #(.width(32)) u_a0 (.D(Data_In), .en(and_4_out), .Q(a0), .clk(Clock), .clr(Clear));
  Register #(.width(32)) u_a1 (.D(Data_In), .en(and_5_out), .Q(a1), .clk(Clock), .clr(Clear));
  Register #(.width(32)) u_a2 (.D(Data_In), .en(and_6_out), .Q(a2), .clk(Clock), .clr(Clear));
  Register #(.width(32)) u_t0 (.D(Data_In), .en(and_7_out), .Q(t0), .clk(Clock), .clr(Clear));
  Register #(.width(32)) u_t1 (.D(Data_In), .en(and_8_out), .Q(t1), .clk(Clock), .clr(Clear));
  Register #(.width(32)) u_t2 (.D(Data_In), .en(and_9_out), .Q(t2), .clk(Clock), .clr(Clear));
  Register #(.width(32)) u_s0 (.D(Data_In), .en(and_10_out), .Q(s0), .clk(Clock), .clr(Clear));
  Register #(.width(32)) u_s1 (.D(Data_In), .en(and_11_out), .Q(s1), .clk(Clock), .clr(Clear));
  Register #(.width(32)) u_s2 (.D(Data_In), .en(and_12_out), .Q(s2), .clk(Clock), .clr(Clear));
  Register #(.width(32)) u_k0 (.D(Data_In), .en(and_13_out), .Q(k0), .clk(Clock), .clr(Clear));
  Register #(.width(32)) u_sp (.D(Data_In), .en(and_14_out), .Q(sp), .clk(Clock), .clr(Clear));
  Register #(.width(32)) pr (.D(Data_In), .en(and_15_out), .Q(fp), .clk(Clock), .clr(Clear));
  Register #(.width(32)) u_ra (.D(Data_In), .en(and_16_out), .Q(ra), .clk(Clock), .clr(Clear));
  Multiplexer #(.select(4), .width(32), .enable("false")) multiplexer_1 (
    .in0(zero), .in1(at), .in2(v0), .in3(a0), .in4(a1), .in5(a2), .in6(t0), .in7(t1), .in8(t2), .in9(s0),
    .in10(s1), .in11(s2), .in12(k0), .in13(sp), .in14(fp), .in15(ra), .out(Data_Out), .sel(RegSel));

  // Other names for the same wires on the sheet: Din[31:0] = Data_In; en = WrReg
endmodule
